// Logisim project CRC.circ as structural Verilog: 2 circuits, main circuit CRC
module CRC (
  input  [7:0] A,
  input  [3:0] B,
  output [10:0] C
);

  wire [2:0] n4bit_div_1_c, n4bit_div_2_c, n4bit_div_3_c, n4bit_div_4_c, n4bit_div_5_c, n4bit_div_6_c;
  wire [3:1] n4bit_div_8_c;

  _4bit_div u_4bit_div_1 (.A(A[7:4]), .B(B), .C(n4bit_div_1_c));  // open: D
  _4bit_div u_4bit_div_2 (.A({n4bit_div_1_c, A[3]}), .B(B), .C(n4bit_div_2_c));  // open: D
  _4bit_div u_4bit_div_3 (.A({n4bit_div_8_c, 1'b0}), .B(B), .C(n4bit_div_3_c));  // open: D
  _4bit_div u_4bit_div_4 (.A({n4bit_div_2_c, A[2]}), .B(B), .C(n4bit_div_4_c));  // open: D
  _4bit_div u_4bit_div_5 (.A({n4bit_div_3_c, 1'b0}), .B(B), .C(n4bit_div_5_c));  // open: D
  _4bit_div u_4bit_div_6 (.A({n4bit_div_4_c, A[1]}), .B(B), .C(n4bit_div_6_c));  // open: D
  _4bit_div u_4bit_div_7 (.A({n4bit_div_5_c, 1'b0}), .B(B), .C(C[2:0]));  // open: D
  _4bit_div u_4bit_div_8 (.A({n4bit_div_6_c, A[0]}), .B(B), .C(n4bit_div_8_c));  // open: D

  assign C[10:3] = A;
endmodule

module _4bit_div (
  input  [3:0] A,
  input  [3:0] B,
  output [2:0] C,
  output D
);

  wire [2:0] xor_1_out;

  xor xor_1 (xor_1_out[0], A[0], B[0]);
  xor xor_2 (xor_1_out[1], A[1], B[1]);
  xor xor_3 (xor_1_out[2], A[2], B[2]);
  Multiplexer #(.width(3), .enable("false")) multiplexer_1 (.in0(A[2:0]), .in1(xor_1_out), .out(C), .sel(A[3]));

  assign D = A[3];
endmodule
