// Logisim project P0-L0-Q1-check.circ as structural Verilog: 2 circuits, main circuit test
module test (
);

  wire and_1_out, clock_1_out, comparator_1_eq, counter_1_carry, not_1_out, not_2_out, s_r_ff_1_q;
  wire [3:0] counter_2_q;
  wire [7:0] counter_1_q;
  wire [10:0] dummy_crc_1_c, dummy_crc_2_c;

  not not_1 (not_1_out, s_r_ff_1_q);
  Clock clock_1 (.out(clock_1_out));
  and and_1 (and_1_out, not_1_out, clock_1_out);
  Counter counter_1 (.Q(counter_1_q), .carry(counter_1_carry), .clk(and_1_out));  // open: load, D, count, clr
  Counter #(.width(4), .max('hf)) counter_2 (
    .count(counter_1_carry), .Q(counter_2_q), .clk(and_1_out));  // open: load, D, carry, clr
  dummy_CRC dummy_crc_1 (.A(counter_1_q), .B(counter_2_q), .C(dummy_crc_1_c));
  dummy_CRC dummy_crc_2 (.A(counter_1_q), .B(counter_2_q), .C(dummy_crc_2_c));
  Comparator #(.width(11)) comparator_1 (.a(dummy_crc_1_c), .b(dummy_crc_2_c), .eq(comparator_1_eq));  // open: gt, lt
  not not_2 (not_2_out, comparator_1_eq);
  S_R_Flip_Flop s_r_ff_1 (
    .S(not_2_out), .clk(and_1_out), .R(1'b0), .Q(s_r_ff_1_q), .en(1'b1));  // open: Qn, preset, reset
  LED led_1 (.in(s_r_ff_1_q));
endmodule

module dummy_CRC (
  input  [7:0] A,
  input  [3:0] B,
  output [10:0] C
);
endmodule
