// Logisim project P0-L0-Q2-check.circ as structural Verilog: 2 circuits, main circuit test
module test (
);

  wire and_1_out, clock_1_out, comparator_1_eq, counter_1_carry, not_1_out, not_2_out, not_3_out, s_r_ff_1_q;
  wire [3:0] dummy_alu_1_c, dummy_alu_2_c;
  wire [9:0] counter_1_q;

  not not_1 (not_1_out, s_r_ff_1_q);
  Clock clock_1 (.out(clock_1_out));
  and and_1 (and_1_out, not_1_out, clock_1_out, not_2_out);
  not not_2 (not_2_out, counter_1_carry);
  Counter #(.width(10), .max('h3ff)) counter_1 (
    .Q(counter_1_q), .carry(counter_1_carry), .clk(and_1_out));  // open: load, D, count, clr
  dummy_ALU dummy_alu_1 (.A(counter_1_q[3:0]), .B(counter_1_q[7:4]), .ALUOp(counter_1_q[9:8]), .C(dummy_alu_1_c));
  dummy_ALU dummy_alu_2 (.A(counter_1_q[3:0]), .B(counter_1_q[7:4]), .ALUOp(counter_1_q[9:8]), .C(dummy_alu_2_c));
  Comparator #(.width(4)) comparator_1 (.a(dummy_alu_1_c), .b(dummy_alu_2_c), .eq(comparator_1_eq));  // open: gt, lt
  not not_3 (not_3_out, comparator_1_eq);
  S_R_Flip_Flop s_r_ff_1 (
    .S(not_3_out), .clk(and_1_out), .R(1'b0), .Q(s_r_ff_1_q), .en(1'b1));  // open: Qn, preset, reset
  LED led_1 (.in(s_r_ff_1_q));
endmodule

module dummy_ALU (
  input  [3:0] A,
  input  [3:0] B,
  input  [1:0] ALUOp,
  output [3:0] C
);
endmodule
