// Logisim project FSM.circ as structural Verilog: 3 circuits, main circuit fsm
module fsm (
  input  CLR,
  input  [1:0] In,
  output Z
);

  wire clock_1_out;
  wire [1:0] multiplexer_1_out, register_1_q, switch_1_out;

  Clock clock_1 (.out(clock_1_out));
  switch switch_1 (.IN(In), .staste(register_1_q), .OUT(switch_1_out));
  Multiplexer #(.width(2), .enable("false")) multiplexer_1 (
    .in0(switch_1_out), .in1(2'b00), .out(multiplexer_1_out), .sel(CLR));
  Register #(.width(2)) register_1 (.D(multiplexer_1_out), .Q(register_1_q), .clk(clock_1_out));  // open: en, clr
  \output  output_1 (.IN(In), .staste(register_1_q), .OUT(Z));
endmodule

module switch (
  input  [1:0] IN,
  input  [1:0] staste,
  output [1:0] OUT
);

  wire and_1_out, and_2_out, and_3_out, and_4_out, and_5_out, and_6_out, and_7_out, not_1_out, not_2_out,
       not_3_out, not_4_out, not_5_out, not_6_out, not_7_out;

  not not_1 (not_1_out, IN[0]);
  not not_2 (not_2_out, staste[1]);
  not not_3 (not_3_out, IN[0]);
  not not_4 (not_4_out, IN[0]);
  and and_1 (and_1_out, not_1_out, not_2_out);
  and and_2 (and_2_out, not_3_out, staste[1]);
  not not_5 (not_5_out, staste[0]);
  and and_3 (and_3_out, not_4_out, staste[1]);
  not not_6 (not_6_out, staste[0]);
  not not_7 (not_7_out, IN[1]);
  and and_4 (and_4_out, and_1_out, staste[0]);
  and and_5 (and_5_out, and_2_out, not_5_out);
  and and_6 (and_6_out, and_3_out, not_6_out);
  and and_7 (and_7_out, not_7_out, IN[0]);
  or or_1 (OUT[1], and_4_out, and_5_out);
  or or_2 (OUT[0], and_6_out, and_7_out);
endmodule

module \output  (
  input  [1:0] IN,
  input  [1:0] staste,
  output OUT
);

  wire and_1_out, and_2_out, and_3_out, and_4_out, and_5_out, and_6_out, and_7_out, not_1_out, not_2_out,
       not_3_out, not_4_out, not_5_out, not_6_out, not_7_out;
  wire [1:0] or_2_out;

  not not_1 (not_1_out, IN[0]);
  not not_2 (not_2_out, staste[1]);
  not not_3 (not_3_out, IN[0]);
  not not_4 (not_4_out, IN[0]);
  and and_1 (and_1_out, not_1_out, not_2_out);
  and and_2 (and_2_out, not_3_out, staste[1]);
  not not_5 (not_5_out, staste[0]);
  and and_3 (and_3_out, not_4_out, staste[1]);
  not not_6 (not_6_out, staste[0]);
  not not_7 (not_7_out, IN[1]);
  and and_4 (and_4_out, and_1_out, staste[0]);
  and and_5 (and_5_out, and_2_out, not_5_out);
  and and_6 (and_6_out, and_3_out, not_6_out);
  and and_7 (and_7_out, not_7_out, IN[0]);
  or or_1 (or_2_out[1], and_4_out, and_5_out);
  or or_2 (or_2_out[0], and_6_out, and_7_out);
  Multiplexer #(.select(2), .enable("false")) multiplexer_1 (
    .in0(1'b0), .in1(1'b0), .in2(1'b0), .in3(1'b1), .out(OUT), .sel(or_2_out));
endmodule
