// Logisim project GRF.circ as structural Verilog: 5 circuits, main circuit grf
module grf (
  input  clk,
  input  reset,
  input  WE,
  input  [4:0] A1,
  input  [4:0] A2,
  input  [4:0] A3,
  input  [31:0] WD,
  output [31:0] RD1,
  output [31:0] RD2
);

  wire [3:0] demultiplexer_1_out0, demultiplexer_1_out1, demultiplexer_2_out0, demultiplexer_2_out1,
       demultiplexer_3_out0, demultiplexer_3_out1;
  wire [31:0] n00_15_1__1, n00_15_1__2, n16_31_1__1, n16_31_1__2;

  Demultiplexer #(.width(4), .enable("false")) demultiplexer_1 (
    .out0(demultiplexer_1_out0), .out1(demultiplexer_1_out1), .in(A2[3:0]), .sel(A2[4]));
  Demultiplexer #(.width(4), .enable("false")) demultiplexer_2 (
    .out0(demultiplexer_2_out0), .out1(demultiplexer_2_out1), .in(A1[3:0]), .sel(A1[4]));
  Demultiplexer #(.width(4)) demultiplexer_3 (
    .out0(demultiplexer_3_out0), .out1(demultiplexer_3_out1), .in(A3[3:0]), .sel(WE), .en(A3[4]));
  _00_15 u_00_15_1 (
    .WD(WD), .clock(clk), .reset(reset), .INPUT(demultiplexer_3_out0), .OUTPUT1(demultiplexer_2_out0),
    .OUTPUT2(demultiplexer_1_out0), ._1(n00_15_1__1), ._2(n00_15_1__2));
  _16_31 u_16_31_1 (
    .WD(WD), .clock(clk), .reset(reset), .INPUT(demultiplexer_3_out1), .OUTPUT1(demultiplexer_2_out1),
    .OUTPUT2(demultiplexer_1_out1), ._1(n16_31_1__1), ._2(n16_31_1__2));
  Multiplexer #(.width(32), .enable("false")) multiplexer_1 (
    .in0(n00_15_1__2), .in1(n16_31_1__2), .out(RD2), .sel(A2[4]));
  Multiplexer #(.width(32), .enable("false")) multiplexer_2 (
    .in0(n00_15_1__1), .in1(n16_31_1__1), .out(RD1), .sel(A1[4]));
endmodule

// 16-31
module _4bit (
  input  [1:0] INPUT,
  input  [1:0] OUTPUT1,
  input  [31:0] WT,
  input  WE,
  input  clock,
  input  reset,
  input  [1:0] OUTPUT2,
  output [31:0] RD1,
  output [31:0] RD2
);

  wire [31:0] _00_q, _01_q, _02_q, _03_q, demultiplexer_1_out0, demultiplexer_1_out1, demultiplexer_1_out2,
       demultiplexer_1_out3;

  // Probe on demultiplexer_1_out0
  Demultiplexer #(.select(2), .width(32), .tristate("true")) demultiplexer_1 (
    .out0(demultiplexer_1_out0), .out1(demultiplexer_1_out1), .out2(demultiplexer_1_out2),
    .out3(demultiplexer_1_out3), .in(WT), .sel(INPUT), .en(WE));
  Register #(.width(32)) _00 (.D(demultiplexer_1_out0), .Q(_00_q), .clk(clock), .clr(reset));  // open: en
  Register #(.width(32)) _01 (.D(demultiplexer_1_out1), .Q(_01_q), .clk(clock), .clr(reset));  // open: en
  Register #(.width(32)) _02 (.D(demultiplexer_1_out2), .Q(_02_q), .clk(clock), .clr(reset));  // open: en
  Register #(.width(32)) _03 (.D(demultiplexer_1_out3), .Q(_03_q), .clk(clock), .clr(reset));  // open: en
  Multiplexer #(.select(2), .width(32), .enable("false")) multiplexer_1 (
    .in0(_00_q), .in1(_01_q), .in2(_02_q), .in3(_03_q), .out(RD1), .sel(OUTPUT1));
  Multiplexer #(.select(2), .width(32), .enable("false")) multiplexer_2 (
    .in0(_00_q), .in1(_01_q), .in2(_02_q), .in3(_03_q), .out(RD2), .sel(OUTPUT2));
endmodule

module _16_31 (
  input  [3:0] INPUT,
  input  [3:0] OUTPUT1,
  input  [3:0] OUTPUT2,
  input  [31:0] WD,
  input  clock,
  input  reset,
  output [31:0] _1,
  output [31:0] _2
);

  wire decoder_1_out0, decoder_1_out1, decoder_1_out2, decoder_1_out3;
  wire [31:0] _00_03_rd1, _00_03_rd2, _04_07_rd1, _04_07_rd2, _08_11_rd1, _08_11_rd2, _12_15_rd1, _12_15_rd2;

  Decoder #(.select(2), .enable("false")) decoder_1 (
    .out0(decoder_1_out0), .out1(decoder_1_out1), .out2(decoder_1_out2), .out3(decoder_1_out3),
    .sel(INPUT[3:2]));
  _4bit _00_03 (
    .WT(WD), .clock(clock), .reset(reset), .RD1(_00_03_rd1), .INPUT(INPUT[1:0]), .OUTPUT1(OUTPUT1[1:0]),
    .WE(decoder_1_out0), .OUTPUT2(OUTPUT2[1:0]), .RD2(_00_03_rd2));
  _4bit _04_07 (
    .WT(WD), .clock(clock), .reset(reset), .RD1(_04_07_rd1), .INPUT(INPUT[1:0]), .OUTPUT1(OUTPUT1[1:0]),
    .WE(decoder_1_out1), .OUTPUT2(OUTPUT2[1:0]), .RD2(_04_07_rd2));
  _4bit _08_11 (
    .WT(WD), .clock(clock), .reset(reset), .RD1(_08_11_rd1), .INPUT(INPUT[1:0]), .OUTPUT1(OUTPUT1[1:0]),
    .WE(decoder_1_out2), .OUTPUT2(OUTPUT2[1:0]), .RD2(_08_11_rd2));
  _4bit _12_15 (
    .WT(WD), .clock(clock), .reset(reset), .RD1(_12_15_rd1), .INPUT(INPUT[1:0]), .OUTPUT1(OUTPUT1[1:0]),
    .WE(decoder_1_out3), .OUTPUT2(OUTPUT2[1:0]), .RD2(_12_15_rd2));
  Multiplexer #(.select(2), .width(32), .enable("false")) multiplexer_1 (
    .in0(_00_03_rd1), .in1(_04_07_rd1), .in2(_08_11_rd1), .in3(_12_15_rd1), .out(_1), .sel(OUTPUT1[3:2]));
  Multiplexer #(.select(2), .width(32), .enable("false")) multiplexer_2 (
    .in0(_00_03_rd2), .in1(_04_07_rd2), .in2(_08_11_rd2), .in3(_12_15_rd2), .out(_2), .sel(OUTPUT2[3:2]));
endmodule

module _00_03 (
  input  [1:0] INPUT,
  input  [1:0] OUTPUT1,
  input  [31:0] WT,
  input  WE,
  input  clock,
  input  reset,
  input  [1:0] OUTPUT2,
  output [31:0] RD1,
  output [31:0] RD2
);

  wire [31:0] _00_q, _01_q, _02_q, _03_q, demultiplexer_1_out0, demultiplexer_1_out1, demultiplexer_1_out2,
       demultiplexer_1_out3;

  // Probe on demultiplexer_1_out0
  Demultiplexer #(.select(2), .width(32), .tristate("true")) demultiplexer_1 (
    .out0(demultiplexer_1_out0), .out1(demultiplexer_1_out1), .out2(demultiplexer_1_out2),
    .out3(demultiplexer_1_out3), .in(WT), .sel(INPUT), .en(WE));
  Register #(.width(32)) _00 (.D(demultiplexer_1_out0), .Q(_00_q), .clk(clock), .clr(1'b1));  // open: en
  Register #(.width(32)) _01 (.D(demultiplexer_1_out1), .Q(_01_q), .clk(clock), .clr(reset));  // open: en
  Register #(.width(32)) _02 (.D(demultiplexer_1_out2), .Q(_02_q), .clk(clock), .clr(reset));  // open: en
  Register #(.width(32)) _03 (.D(demultiplexer_1_out3), .Q(_03_q), .clk(clock), .clr(reset));  // open: en
  Multiplexer #(.select(2), .width(32), .enable("false")) multiplexer_1 (
    .in0(_00_q), .in1(_01_q), .in2(_02_q), .in3(_03_q), .out(RD1), .sel(OUTPUT1));
  Multiplexer #(.select(2), .width(32), .enable("false")) multiplexer_2 (
    .in0(_00_q), .in1(_01_q), .in2(_02_q), .in3(_03_q), .out(RD2), .sel(OUTPUT2));
endmodule

module _00_15 (
  input  [3:0] INPUT,
  input  [3:0] OUTPUT1,
  input  [3:0] OUTPUT2,
  input  [31:0] WD,
  input  clock,
  input  reset,
  output [31:0] _1,
  output [31:0] _2
);

  wire decoder_1_out0, decoder_1_out1, decoder_1_out2, decoder_1_out3;
  wire [31:0] _04_07_rd1, _04_07_rd2, _08_11_rd1, _08_11_rd2, _12_15_rd1, _12_15_rd2, n00_03_1_rd1,
       n00_03_1_rd2;

  Decoder #(.select(2), .enable("false")) decoder_1 (
    .out0(decoder_1_out0), .out1(decoder_1_out1), .out2(decoder_1_out2), .out3(decoder_1_out3),
    .sel(INPUT[3:2]));
  _00_03 u_00_03_1 (
    .WT(WD), .clock(clock), .reset(reset), .RD1(n00_03_1_rd1), .RD2(n00_03_1_rd2), .INPUT(INPUT[1:0]),
    .OUTPUT1(OUTPUT1[1:0]), .WE(decoder_1_out0), .OUTPUT2(OUTPUT2[1:0]));
  _4bit _04_07 (
    .WT(WD), .clock(clock), .reset(reset), .RD1(_04_07_rd1), .INPUT(INPUT[1:0]), .OUTPUT1(OUTPUT1[1:0]),
    .WE(decoder_1_out1), .OUTPUT2(OUTPUT2[1:0]), .RD2(_04_07_rd2));
  _4bit _08_11 (
    .WT(WD), .clock(clock), .reset(reset), .RD1(_08_11_rd1), .INPUT(INPUT[1:0]), .OUTPUT1(OUTPUT1[1:0]),
    .WE(decoder_1_out2), .OUTPUT2(OUTPUT2[1:0]), .RD2(_08_11_rd2));
  _4bit _12_15 (
    .WT(WD), .clock(clock), .reset(reset), .RD1(_12_15_rd1), .INPUT(INPUT[1:0]), .OUTPUT1(OUTPUT1[1:0]),
    .WE(decoder_1_out3), .OUTPUT2(OUTPUT2[1:0]), .RD2(_12_15_rd2));
  Multiplexer #(.select(2), .width(32), .enable("false")) multiplexer_1 (
    .in0(n00_03_1_rd1), .in1(_04_07_rd1), .in2(_08_11_rd1), .in3(_12_15_rd1), .out(_1), .sel(OUTPUT1[3:2]));
  Multiplexer #(.select(2), .width(32), .enable("false")) multiplexer_2 (
    .in0(n00_03_1_rd2), .in1(_04_07_rd2), .in2(_08_11_rd2), .in3(_12_15_rd2), .out(_2), .sel(OUTPUT2[3:2]));
endmodule
