// Logisim project alu.circ as structural Verilog: 1 circuit, main circuit alu
module alu (
  input  [3:0] A,
  input  [3:0] B,
  input  [1:0] Op,
  output [3:0] C
);

  wire [3:0] tunnel, tunnel_t, tunnel_t_t, tunnel_t_t_t;

  Adder #(.width(4)) adder_1 (.a(A), .b(B), .out(tunnel_t));  // open: cin, cout
  Subtractor #(.width(4)) subtractor_1 (.a(A), .b(B), .out(tunnel_t_t));  // open: bin, bout
  assign tunnel = A & B;  // AND_Gate and_1, 4 bits wide
  assign tunnel_t_t_t = A | B;  // OR_Gate or_1, 4 bits wide
  Multiplexer #(.select(2), .width(4), .enable("false")) multiplexer_1 (
    .in0(tunnel_t), .in1(tunnel_t_t), .in2(tunnel), .in3(tunnel_t_t_t), .out(C), .sel(Op));
endmodule
