// Logisim project MAIN.circ as structural Verilog: 8 circuits, main circuit main
module main (
  input  in_1,
  output [31:0] out_2,
  output out_3,
  output [4:0] out_4,
  output [31:0] out_5,
  output out_6,
  output [4:0] out_7,
  output [31:0] out_8
);

  wire ALUSrc, clk, EXTOp, JalSrc, MemRead, RegDst, Zero;
  wire [1:0] Branch, MemtoReg;
  wire [2:0] alucontrol_1_aluopre, ALUOp;
  wire [2:2] NewBranch;
  wire [4:0] multiplexer_2_out;
  wire [31:0] dm_1_readdata, multiplexer_3_out, multiplexer_4_out, offset, pc_4, RD1, Result;

  Clock clock_1 (.out(clk));
  IFU ifu_1 (
    .instr(out_2), .clk(clk), .reset(in_1), .zero(Zero), .branch({NewBranch[2], Branch}), .pc_4(pc_4),
    .offset(offset), .address26(out_2[25:0]), .jrinput({Result[31:7], out_7, Result[1:0]}));
  Controller controller_1 (
    .Op(out_2[31:26]), .RegDst(RegDst), .ALUSrc(ALUSrc), .MemtoReg(MemtoReg), .RegWrite(out_3),
    .MemRead(MemRead), .MemWrite(out_6), .Branch(Branch), .EXTOp(EXTOp), .ALUOp(ALUOp), .jalbranch(JalSrc));
  Multiplexer #(.width(5), .enable("false")) multiplexer_1 (
    .in0(out_2[20:16]), .in1(out_2[15:11]), .out(out_4), .sel(RegDst));
  EXT ext_1 (.imm16(out_2[15:0]), .EXTOp(EXTOp), .imm32(offset));
  Multiplexer #(.width(5), .disabled(0), .enable("false")) multiplexer_2 (
    .in0(out_4), .in1({5{1'b1}}), .out(multiplexer_2_out), .sel(JalSrc));
  Multiplexer #(.width(32), .disabled(0), .enable("false")) multiplexer_3 (
    .in0(out_5), .in1(pc_4), .out(multiplexer_3_out), .sel(JalSrc));
  GRF grf_1 (
    .A1(out_2[25:21]), .A2(out_2[20:16]), .A3(multiplexer_2_out), .WD(multiplexer_3_out), .RD1(RD1),
    .RD2(out_8), .clk(clk), .reset(in_1), .WE(out_3));
  Multiplexer #(.width(32), .enable("false")) multiplexer_4 (
    .in0(out_8), .in1(offset), .out(multiplexer_4_out), .sel(ALUSrc));
  ALUcontrol alucontrol_1 (.ALUOp(ALUOp), .Func(out_2[5:0]), .ALUopre(alucontrol_1_aluopre), .jrbranch(NewBranch[2]));
  ALU alu_1 (
    .A(RD1), .B(multiplexer_4_out), .Zero(Zero), .Result({Result[31:7], out_7, Result[1:0]}),
    .ALUoperation(alucontrol_1_aluopre));
  DM dm_1 (
    .Address(out_7), .WriteData(out_8), .ReadData(dm_1_readdata), .MemRead(MemRead), .MemWrite(out_6),
    .clk(clk), .reset(in_1));
  Multiplexer #(.select(2), .width(32), .disabled(0), .enable("false")) multiplexer_5 (
    .in0({Result[31:7], out_7, Result[1:0]}), .in1(dm_1_readdata), .in2({out_2[15:0], {16{1'b0}}}),
    .out(out_5), .sel(MemtoReg));  // open: in3

  // Other names for the same wires on the sheet: add26[25:0] = out_2[25:0]; Funct[5:0] = out_2[5:0];
  //   imm16[15:0] = out_2[15:0]; Instr[31:0] = out_2; Shamt[4:0] = out_2[10:6]; Rd[4:0] = out_2[15:11];
  //   Rt[4:0] = out_2[20:16]; Rs[4:0] = out_2[25:21]; Op[5:0] = out_2[31:26]; MemWrite = out_6;
  //   NewBranch[1:0] = Branch; MemData[31:0] = out_8; RD2[31:0] = out_8; RegAddr[4:0] = out_4; RegData[31:0] = out_5;
  //   RegWrite = out_3; Reset = in_1; MemAddr[4:0] = out_7; Result[6:2] = out_7
endmodule

module IFU (
  input  [2:0] branch,
  input  zero,
  input  clk,
  input  reset,
  input  [31:0] jrinput,
  input  [25:0] address26,
  input  [31:0] offset,
  output [31:0] pc_4,
  output [31:0] instr
);

  wire and_1_out;
  wire [27:0] bit_extender_1_out, shifter_2_out;
  wire [31:0] adder_2_out, multiplexer_1_out, multiplexer_2_out, PC, PC_q, shifter_1_out;

  Register #(.width(32)) u_PC (.D(PC), .Q(PC_q), .clk(clk), .clr(reset));  // open: en
  Adder #(.width(32)) adder_1 (.a(32'h4), .b(PC_q), .out(pc_4));  // open: cin, cout
  Shifter #(.width(32)) shifter_1 (.in(offset), .\dist (5'b00010), .out(shifter_1_out));
  assign bit_extender_1_out = {{2{1'b0}}, address26};  // Bit_Extender bit_extender_1
  ROM #(.addrWidth(5), .dataWidth(32)) rom_1 (.addr(PC_q[6:2]), .data(instr));  // open: sel
  Adder #(.width(32)) adder_2 (.a(pc_4), .b(shifter_1_out), .out(adder_2_out));  // open: cin, cout
  Shifter #(.width(28)) shifter_2 (.in(bit_extender_1_out), .\dist (5'b00010), .out(shifter_2_out));
  and and_1 (and_1_out, branch[0], zero);
  Multiplexer #(.width(32), .disabled(0), .enable("false")) multiplexer_1 (
    .in0(pc_4), .in1(adder_2_out), .out(multiplexer_1_out), .sel(and_1_out));
  Multiplexer #(.width(32), .enable("false")) multiplexer_2 (
    .in0(multiplexer_1_out), .in1({pc_4[31:28], shifter_2_out}), .out(multiplexer_2_out), .sel(branch[1]));
  Multiplexer #(.width(32), .disabled(0), .enable("false")) multiplexer_3 (
    .in0(multiplexer_2_out), .in1(jrinput), .out(PC), .sel(branch[2]));

  // Other names for the same wires on the sheet: add26[25:0] = address26; b0 = branch[0]; b1 = branch[1];
  //   b2 = branch[2]; jradd[31:0] = jrinput

  // Notes on the sheet:
  //   contents of rom_1 (hex, n*v repeats v):
  //   34100007 34110007 c000c05 3411000f 8000c09 12110001 3412000f 34140001 3e00008 2329821
endmodule

module GRF (
  input  clk,
  input  reset,
  input  WE,
  input  [4:0] A1,
  input  [4:0] A2,
  input  [4:0] A3,
  input  [31:0] WD,
  output [31:0] RD1,
  output [31:0] RD2
);

  wire [31:0] _00, _01, _02, _03, _04, _05, _06, _07, _08, _09, _10, _11, _12, _13, _14, _15, _16, _17, _18,
       _19, _20, _21, _22, _23, _24, _25, _26, _27, _28, _29, _30, _31, and_1_out, in00, in01, in02, in03,
       in04, in05, in06, in07, in08, in09, in10, in11, in12, in13, in14, in15, in16, in17, in18, in19, in20,
       in21, in22, in23, in24, in25, in26, in27, in28, in29, in30, in31;

  Demultiplexer #(.select(5), .width(32), .tristate("true"), .enable("false")) demultiplexer_1 (
    .out0(in00), .out1(in01), .out2(in02), .out3(in03), .out4(in04), .out5(in05), .out6(in06), .out7(in07),
    .out8(in08), .out9(in09), .out10(in10), .out11(in11), .out12(in12), .out13(in13), .out14(in14),
    .out15(in15), .out16(in16), .out17(in17), .out18(in18), .out19(in19), .out20(in20), .out21(in21),
    .out22(in22), .out23(in23), .out24(in24), .out25(in25), .out26(in26), .out27(in27), .out28(in28),
    .out29(in29), .out30(in30), .out31(in31), .in(WD), .sel(A3));
  assign and_1_out = {32{1'b0}} & in00;  // AND_Gate and_1, 32 bits wide
  Register #(.width(32)) register_1 (.D(and_1_out), .en(WE), .Q(_00), .clk(clk), .clr(reset));
  Register #(.width(32)) register_2 (.D(in08), .en(WE), .Q(_08), .clk(clk), .clr(reset));
  Register #(.width(32)) register_3 (.D(in16), .en(WE), .Q(_16), .clk(clk), .clr(reset));
  Register #(.width(32)) register_4 (.D(in24), .en(WE), .Q(_24), .clk(clk), .clr(reset));
  Register #(.width(32)) register_5 (.D(in01), .en(WE), .Q(_01), .clk(clk), .clr(reset));
  Register #(.width(32)) register_6 (.D(in09), .en(WE), .Q(_09), .clk(clk), .clr(reset));
  Register #(.width(32)) register_7 (.D(in17), .en(WE), .Q(_17), .clk(clk), .clr(reset));
  Register #(.width(32)) register_8 (.D(in25), .en(WE), .Q(_25), .clk(clk), .clr(reset));
  Multiplexer #(.select(5), .width(32), .enable("false")) multiplexer_1 (
    .in0(_00), .in1(_01), .in2(_02), .in3(_03), .in4(_04), .in5(_05), .in6(_06), .in7(_07), .in8(_08),
    .in9(_09), .in10(_10), .in11(_11), .in12(_12), .in13(_13), .in14(_14), .in15(_15), .in16(_16),
    .in17(_17), .in18(_18), .in19(_19), .in20(_20), .in21(_21), .in22(_22), .in23(_23), .in24(_24),
    .in25(_25), .in26(_26), .in27(_27), .in28(_28), .in29(_29), .in30(_30), .in31(_31), .out(RD1), .sel(A1));
  Register #(.width(32)) register_9 (.D(in02), .en(WE), .Q(_02), .clk(clk), .clr(reset));
  Register #(.width(32)) register_10 (.D(in10), .en(WE), .Q(_10), .clk(clk), .clr(reset));
  Register #(.width(32)) register_11 (.D(in18), .en(WE), .Q(_18), .clk(clk), .clr(reset));
  Register #(.width(32)) register_12 (.D(in26), .en(WE), .Q(_26), .clk(clk), .clr(reset));
  Register #(.width(32)) register_13 (.D(in03), .en(WE), .Q(_03), .clk(clk), .clr(reset));
  Register #(.width(32)) register_14 (.D(in11), .en(WE), .Q(_11), .clk(clk), .clr(reset));
  Register #(.width(32)) register_15 (.D(in19), .en(WE), .Q(_19), .clk(clk), .clr(reset));
  Register #(.width(32)) register_16 (.D(in27), .en(WE), .Q(_27), .clk(clk), .clr(reset));
  Multiplexer #(.select(5), .width(32), .enable("false")) multiplexer_2 (
    .in0(_00), .in1(_01), .in2(_02), .in3(_03), .in4(_04), .in5(_05), .in6(_06), .in7(_07), .in8(_08),
    .in9(_09), .in10(_10), .in11(_11), .in12(_12), .in13(_13), .in14(_14), .in15(_15), .in16(_16),
    .in17(_17), .in18(_18), .in19(_19), .in20(_20), .in21(_21), .in22(_22), .in23(_23), .in24(_24),
    .in25(_25), .in26(_26), .in27(_27), .in28(_28), .in29(_29), .in30(_30), .in31(_31), .out(RD2), .sel(A2));
  Register #(.width(32)) register_17 (.D(in04), .en(WE), .Q(_04), .clk(clk), .clr(reset));
  Register #(.width(32)) register_18 (.D(in12), .en(WE), .Q(_12), .clk(clk), .clr(reset));
  Register #(.width(32)) register_19 (.D(in20), .en(WE), .Q(_20), .clk(clk), .clr(reset));
  Register #(.width(32)) register_20 (.D(in28), .en(WE), .Q(_28), .clk(clk), .clr(reset));
  Register #(.width(32)) register_21 (.D(in05), .en(WE), .Q(_05), .clk(clk), .clr(reset));
  Register #(.width(32)) register_22 (.D(in13), .en(WE), .Q(_13), .clk(clk), .clr(reset));
  Register #(.width(32)) register_23 (.D(in21), .en(WE), .Q(_21), .clk(clk), .clr(reset));
  Register #(.width(32)) register_24 (.D(in29), .en(WE), .Q(_29), .clk(clk), .clr(reset));
  Register #(.width(32)) register_25 (.D(in06), .en(WE), .Q(_06), .clk(clk), .clr(reset));
  Register #(.width(32)) register_26 (.D(in14), .en(WE), .Q(_14), .clk(clk), .clr(reset));
  Register #(.width(32)) register_27 (.D(in22), .en(WE), .Q(_22), .clk(clk), .clr(reset));
  Register #(.width(32)) register_28 (.D(in30), .en(WE), .Q(_30), .clk(clk), .clr(reset));
  Register #(.width(32)) register_29 (.D(in07), .en(WE), .Q(_07), .clk(clk), .clr(reset));
  Register #(.width(32)) register_30 (.D(in15), .en(WE), .Q(_15), .clk(clk), .clr(reset));
  Register #(.width(32)) register_31 (.D(in23), .en(WE), .Q(_23), .clk(clk), .clr(reset));
  Register #(.width(32)) register_32 (.D(in31), .en(WE), .Q(_31), .clk(clk), .clr(reset));
endmodule

module ALU (
  input  [31:0] A,
  input  [31:0] B,
  input  [2:0] ALUoperation,
  output [31:0] Result,
  output Zero
);

  wire comparator_1_gt;
  wire [31:0] A_B, A_B_t, A_B_t_t, A_B_t_t_t, A_B_t_t_t_t;

  Adder #(.width(32)) adder_1 (.a(A), .b(B), .out(A_B_t));  // open: cin, cout
  Subtractor #(.width(32)) subtractor_1 (.a(A), .b(B), .out(A_B_t_t));  // open: bin, bout
  Comparator #(.width(32)) comparator_1 (.a(A), .b(B), .gt(comparator_1_gt), .eq(Zero));  // open: lt
  assign A_B = A & B;  // AND_Gate and_1, 32 bits wide
  assign A_B_t_t_t_t = A | B;  // OR_Gate or_1, 32 bits wide
  assign A_B_t_t_t = {{31{1'b0}}, comparator_1_gt};  // Bit_Extender bit_extender_1
  Multiplexer #(.select(3), .width(32), .enable("false")) multiplexer_1 (
    .in0(A_B), .in1(A_B_t_t_t_t), .in2(A_B_t), .in3(A_B_t_t), .in4(A_B_t_t_t), .in5(A), .out(Result),
    .sel(ALUoperation));  // open: in6, in7
endmodule

module DM (
  input  MemRead,
  input  MemWrite,
  input  [4:0] Address,
  input  [31:0] WriteData,
  input  clk,
  input  reset,
  output [31:0] ReadData
);

  RAM #(.addrWidth(5), .dataWidth(32), .bus("separate")) ram_1 (
    .addr(Address), .din(WriteData), .data(ReadData), .str(MemWrite), .sel(1'b1), .clk(clk), .ld(MemRead),
    .clr(reset));
endmodule

module EXT (
  input  EXTOp,
  input  [15:0] imm16,
  output [31:0] imm32
);

  wire [31:0] bit_extender_1_out, bit_extender_2_out;

  assign bit_extender_1_out = {{16{imm16[15]}}, imm16};  // Bit_Extender bit_extender_1
  assign bit_extender_2_out = {{16{1'b0}}, imm16};  // Bit_Extender bit_extender_2
  Multiplexer #(.width(32), .disabled(0), .enable("false")) multiplexer_1 (
    .in0(bit_extender_1_out), .in1(bit_extender_2_out), .out(imm32), .sel(EXTOp));
endmodule

module Controller (
  input  [5:0] Op,
  output RegDst,
  output ALUSrc,
  output [1:0] MemtoReg,
  output RegWrite,
  output MemRead,
  output MemWrite,
  output [1:0] Branch,
  output EXTOp,
  output [2:0] ALUOp,
  output jalbranch
);

  wire _0_0, _1_0, _2_0, _3_0, _4_0, _5_0, j;

  not not_1 (_0_0, Op[0]);
  not not_2 (_1_0, Op[1]);
  not not_3 (_2_0, Op[2]);
  not not_4 (_3_0, Op[3]);
  not not_5 (_4_0, Op[4]);
  not not_6 (_5_0, Op[5]);
  and R_format (RegDst, _5_0, _4_0, _3_0, _2_0, _1_0, _0_0);
  or or_1 (Branch[1], j, jalbranch);
  and lw (MemRead, Op[5], _4_0, _3_0, _2_0, Op[1], Op[0]);
  or or_2 (ALUSrc, ALUOp[2], MemRead, MemWrite);
  or or_3 (RegWrite, RegDst, MemtoReg[1], jalbranch, ALUOp[2], MemRead);
  or or_4 (ALUOp[1], Branch[0], ALUOp[2], MemtoReg[1], j, jalbranch);
  or or_5 (ALUOp[0], MemRead, MemWrite, ALUOp[2], MemtoReg[1], j, jalbranch);
  and sw (MemWrite, Op[5], _4_0, Op[3], _2_0, Op[1], Op[0]);
  and beq (Branch[0], _5_0, _4_0, _3_0, Op[2], _1_0, _0_0);
  and ori (ALUOp[2], _5_0, _4_0, Op[3], Op[2], _1_0, Op[0]);
  and lui (MemtoReg[1], _5_0, _4_0, Op[3], Op[2], Op[1], Op[0]);
  and u_j (j, _5_0, _4_0, _3_0, _2_0, Op[1], _0_0);
  and jal (jalbranch, _5_0, _4_0, _3_0, _2_0, Op[1], Op[0]);

  assign EXTOp = ALUOp[2];
  assign MemtoReg[0] = MemRead;

  // Other names for the same wires on the sheet: ori = ALUOp[2]; beq = Branch[0]; jal = jalbranch; lw = MemRead;
  //   lui = MemtoReg[1]; _0_1 = Op[0]; _1_1 = Op[1]; _2_1 = Op[2]; _3_1 = Op[3]; _4_1 = Op[4]; _5_1 = Op[5];
  //   R = RegDst; sw = MemWrite
endmodule

module ALUcontrol (
  input  [2:0] ALUOp,
  input  [5:0] Func,
  output [2:0] ALUopre,
  output jrbranch
);

  wire _0_0, _1_0, _2_0, _3_0, _4_0, _5_0, addu, beq, lui, lw_sw, not_1_out, not_2_out, not_3_out, ori, subu;

  not not_1 (not_1_out, ALUOp[0]);
  not not_2 (not_2_out, ALUOp[1]);
  not not_3 (not_3_out, ALUOp[2]);
  not not_4 (_0_0, Func[0]);
  not not_5 (_1_0, Func[1]);
  not not_6 (_2_0, Func[2]);
  not not_7 (_3_0, Func[3]);
  not not_8 (_4_0, Func[4]);
  not not_9 (_5_0, Func[5]);
  and u_lw_sw (lw_sw, not_3_out, not_2_out, ALUOp[0]);
  and u_beq (beq, not_3_out, ALUOp[1], not_1_out);
  and u_ori (ori, ALUOp[2], ALUOp[1], ALUOp[0]);
  or or_1 (ALUopre[2], lui, jrbranch);
  or or_2 (ALUopre[1], lw_sw, beq, lui, addu, subu);
  or or_3 (ALUopre[0], beq, jrbranch, ori, subu, lui);
  and lui_j (lui, not_3_out, ALUOp[1], ALUOp[0]);
  and u_addu (addu, not_3_out, not_2_out, not_1_out, Func[5], _4_0, _3_0, _2_0, _1_0, Func[0]);
  and u_subu (subu, not_3_out, not_2_out, not_1_out, Func[5], _4_0, _3_0, _2_0, Func[1], Func[0]);
  and jr (jrbranch, Func[3], _0_0, _4_0, _1_0, _5_0, _2_0);

  // Other names for the same wires on the sheet: _0_1 = Func[0]; _1_1 = Func[1]; _2_1 = Func[2]; _3_1 = Func[3];
  //   _4_1 = Func[4]; _5_1 = Func[5]; jr = jrbranch
endmodule
